# Fritzing sketch Schematics (saved by Fritzing 0.9.3b)
breadboards: 2

parts:
  Part1 = Arduino Uno (Rev3)
  DI1 = 7-Segment LED Display [package=THT]
  U1 = MLX90614 [package=to-39]  # not connected
  C1 = Tantalum Capacitor [capacitance=1μF package="100 mil [THT, tantalum]"]
  C2 = Tantalum Capacitor [capacitance=1μF package="100 mil [THT, tantalum]"]
  C3 = Tantalum Capacitor [capacitance=1μF package="100 mil [THT, tantalum]"]
  R1 = Resistor [tolerance=±5% resistance=220 package=THT]
  R2 = Resistor [tolerance=±5% resistance=220 package=THT]
  R3 = Resistor [tolerance=±5% resistance=220 package=THT]
  J1 = Piezo Speaker
  S1 = Toggle Switch [package=THT]

nets:
  N1: Part1.D8, DI1.cathodeE
  N2: Part1.D9_PWM, DI1.cathodeF
  N3: Part1.D10_PWM/SS, DI1.cathodeG
  N4: Part1.D11_PWM/MOSI, R1.Pin_1
  N5: Part1.D12/MISO, R2.Pin_1
  N6: Part1.D13/SCK, R3.Pin_1
  N7: Part1.GND, C1.-, C2.-, C3.-, J1.pin1, S1.L1
  N8: Part1.D2, J1.pin2
  N9: Part1.D3_PWM, S1.COM
  N10: Part1.D4, DI1.cathodeA
  N11: Part1.D5_PWM, DI1.cathodeB
  N12: Part1.D6_PWM, DI1.cathodeC
  N13: Part1.D7, DI1.cathodeD
  N14: Part1.5V, DI1.commAnode, S1.L2
  N15: C1.+, R1.Pin_0
  N16: C2.+, R2.Pin_0
  N17: C3.+, R3.Pin_0
